# Fritzing sketch Diagrama (saved by Fritzing 0.9.3b)

parts:
  hc-sr1 = hc-sr04
  OLED_I2C1 = OLED 128x64 I2C Monochrome Display
  U3 = ESP 32 DEVKIT DOIT

nets:
  VCC: hc-sr1.VCC, U3.Vin
  N1: hc-sr1.Trig, U3.D25
  N2: hc-sr1.Echo, U3.D33
  GND: hc-sr1.GND, U3.GND
  N3: OLED_I2C1.SDA, U3.D21
  VDD: OLED_I2C1.SCK, OLED_I2C1.VDD, U3.D22, U3.D2, U3.3V3
